// Digital circuit AND.dig as structural Verilog
module AND (
  input  A,
  input  B,
  output S
);

  wire nand_1_out;

  nand nand_1 (nand_1_out, A, B);
  nand nand_2 (S, nand_1_out, nand_1_out);
endmodule
