// Digital circuit BIGXOR.dig as structural Verilog
module BIGXOR (
  input  S_S0,
  input  B0,
  input  S_S1,
  input  B1,
  input  S_S2,
  input  B2,
  input  S_S3,
  input  B3,
  input  S_S4,
  input  B4,
  input  S_S5,
  input  B5,
  input  S_S6,
  input  B6,
  input  S_S7,
  input  B7,
  output SB0,
  output SB1,
  output SB2,
  output SB3,
  output SB4,
  output SB5,
  output SB6,
  output SB7
);

  wire nand_1_out, nand_2_out, nand_3_out, nand_4_out, nand_5_out, nand_6_out, nand_7_out, nand_8_out,
       nand_9_out, nand_10_out, nand_11_out, nand_12_out, nand_13_out, nand_14_out, nand_15_out, nand_16_out,
       nand_17_out, nand_18_out, nand_19_out, nand_20_out, nand_21_out, nand_22_out, nand_23_out, nand_24_out;

  nand nand_1 (nand_1_out, S_S0, B0);
  nand nand_2 (nand_2_out, S_S1, B1);
  nand nand_3 (nand_3_out, S_S2, B2);
  nand nand_4 (nand_4_out, S_S3, B3);
  nand nand_5 (nand_5_out, S_S4, B4);
  nand nand_6 (nand_6_out, S_S5, B5);
  nand nand_7 (nand_7_out, S_S6, B6);
  nand nand_8 (nand_8_out, S_S7, B7);
  nand nand_9 (nand_9_out, S_S0, nand_1_out);
  nand nand_10 (nand_10_out, nand_1_out, B0);
  nand nand_11 (nand_11_out, S_S1, nand_2_out);
  nand nand_12 (nand_12_out, nand_2_out, B1);
  nand nand_13 (nand_13_out, S_S2, nand_3_out);
  nand nand_14 (nand_14_out, nand_3_out, B2);
  nand nand_15 (nand_15_out, S_S3, nand_4_out);
  nand nand_16 (nand_16_out, nand_4_out, B3);
  nand nand_17 (nand_17_out, S_S4, nand_5_out);
  nand nand_18 (nand_18_out, nand_5_out, B4);
  nand nand_19 (nand_19_out, S_S5, nand_6_out);
  nand nand_20 (nand_20_out, nand_6_out, B5);
  nand nand_21 (nand_21_out, S_S6, nand_7_out);
  nand nand_22 (nand_22_out, nand_7_out, B6);
  nand nand_23 (nand_23_out, S_S7, nand_8_out);
  nand nand_24 (nand_24_out, nand_8_out, B7);
  nand nand_25 (SB0, nand_9_out, nand_10_out);
  nand nand_26 (SB1, nand_11_out, nand_12_out);
  nand nand_27 (SB2, nand_13_out, nand_14_out);
  nand nand_28 (SB3, nand_15_out, nand_16_out);
  nand nand_29 (SB4, nand_17_out, nand_18_out);
  nand nand_30 (SB5, nand_19_out, nand_20_out);
  nand nand_31 (SB6, nand_21_out, nand_22_out);
  nand nand_32 (SB7, nand_23_out, nand_24_out);
endmodule
