// Digital circuit FA.dig as structural Verilog
module FA (
  input  A,
  input  B,
  input  Cin,
  output Cout,
  output S
);

  wire and_1_s, and_2_s, xor_1_s;

  XOR xor_1 (.A(A), .B(B), .S(xor_1_s));
  AND and_1 (.A(xor_1_s), .B(Cin), .S(and_1_s));
  AND and_2 (.A(A), .B(B), .S(and_2_s));
  XOR xor_2 (.A(xor_1_s), .B(Cin), .S(S));
  OR or_1 (.A(and_1_s), .B(and_2_s), .S(Cout));
endmodule
