// Digital circuit OR.dig as structural Verilog
module OR (
  input  A,
  input  B,
  output S
);

  wire nand_1_out, nand_2_out;

  nand nand_1 (nand_1_out, A, A);
  nand nand_2 (nand_2_out, B, B);
  nand nand_3 (S, nand_1_out, nand_2_out);
endmodule
