// Digital circuit Somador8bits.dig as structural Verilog
module Somador8bits (
  input  B7,
  input  A7,
  input  B6,
  input  B5,
  input  B4,
  input  B3,
  input  B2,
  input  B1,
  input  B0,
  input  A6,
  input  A5,
  input  A4,
  input  A3,
  input  A2,
  input  A1,
  input  A0,
  input  S_S,
  output S0,
  output S1,
  output S2,
  output S3,
  output S4,
  output S5,
  output S6,
  output S7,
  output Ov
);

  wire fa_2_cout, fa_3_cout, fa_4_cout, fa_5_cout, fa_6_cout, fa_7_cout, fa_8_cout;

  FA fa_1 (.A(A7), .B(B7), .Cin(fa_2_cout), .Cout(Ov), .S(S7));
  FA fa_2 (.A(A6), .B(B6), .Cin(fa_3_cout), .Cout(fa_2_cout), .S(S6));
  FA fa_3 (.A(A5), .B(B5), .Cin(fa_4_cout), .Cout(fa_3_cout), .S(S5));
  FA fa_4 (.A(A4), .B(B4), .Cin(fa_5_cout), .Cout(fa_4_cout), .S(S4));
  FA fa_5 (.A(A3), .B(B3), .Cin(fa_6_cout), .Cout(fa_5_cout), .S(S3));
  FA fa_6 (.A(A2), .B(B2), .Cin(fa_7_cout), .Cout(fa_6_cout), .S(S2));
  FA fa_7 (.A(A1), .B(B1), .Cin(fa_8_cout), .Cout(fa_7_cout), .S(S1));
  FA fa_8 (.A(A0), .B(B0), .Cin(S_S), .Cout(fa_8_cout), .S(S0));
endmodule
