// Digital circuit Somasub.dig as structural Verilog
module Somasub (
  input  A7,
  input  A6,
  input  A5,
  input  A4,
  input  A3,
  input  A2,
  input  A1,
  input  A0,
  input  B7,
  input  B6,
  input  B5,
  input  B4,
  input  B3,
  input  B2,
  input  B1,
  input  B0,
  input  Soma_Sub,
  output S7,
  output S6,
  output S5,
  output S4,
  output S3,
  output S2,
  output S1,
  output S0,
  output Ov
);

  wire bigxor_1_sb0, bigxor_1_sb1, bigxor_1_sb2, bigxor_1_sb3, bigxor_1_sb4, bigxor_1_sb5, bigxor_1_sb6,
       bigxor_1_sb7;

  Somador8bits somador8bits_1 (
    .B7(bigxor_1_sb7), .A7(A7), .B6(bigxor_1_sb6), .B5(bigxor_1_sb5), .B4(bigxor_1_sb4), .B3(bigxor_1_sb3),
    .B2(bigxor_1_sb2), .B1(bigxor_1_sb1), .B0(bigxor_1_sb0), .A6(A6), .A5(A5), .A4(A4), .A3(A3), .A2(A2),
    .A1(A1), .A0(A0), .S_S(Soma_Sub), .S0(S0), .S1(S1), .S2(S2), .S3(S3), .S4(S4), .S5(S5), .S6(S6), .S7(S7),
    .Ov(Ov));
  BIGXOR bigxor_1 (
    .S_S0(Soma_Sub), .B0(B0), .S_S1(Soma_Sub), .B1(B1), .S_S2(Soma_Sub), .B2(B2), .S_S3(Soma_Sub), .B3(B3),
    .S_S4(Soma_Sub), .B4(B4), .S_S5(Soma_Sub), .B5(B5), .S_S6(Soma_Sub), .B6(B6), .S_S7(Soma_Sub), .B7(B7),
    .SB0(bigxor_1_sb0), .SB1(bigxor_1_sb1), .SB2(bigxor_1_sb2), .SB3(bigxor_1_sb3), .SB4(bigxor_1_sb4),
    .SB5(bigxor_1_sb5), .SB6(bigxor_1_sb6), .SB7(bigxor_1_sb7));
endmodule
