// Digital circuit TrabalhoFinal.dig as structural Verilog
module TrabalhoFinal (
  input  A7,
  input  A6,
  input  A5,
  input  A4,
  input  A3,
  input  A2,
  input  A1,
  input  A0,
  input  B7,
  input  B6,
  input  B5,
  input  B4,
  input  B3,
  input  B2,
  input  B1,
  input  B0,
  input  \Soma_Subtração ,
  output Overflow,
  output S7,
  output S6,
  output S5,
  output S4,
  output S3,
  output S2,
  output S1,
  output S0
);

  Somasub somasub_1 (
    .A7(A7), .A6(A6), .A5(A5), .A4(A4), .A3(A3), .A2(A2), .A1(A1), .A0(A0), .B7(B7), .B6(B6), .B5(B5),
    .B4(B4), .B3(B3), .B2(B2), .B1(B1), .B0(B0), .Soma_Sub(\Soma_Subtração ), .S7(S7), .S6(S6), .S5(S5),
    .S4(S4), .S3(S3), .S2(S2), .S1(S1), .S0(S0), .Ov(Overflow));
endmodule
