// Digital circuit ET2+1.dig as structural Verilog
module ET2_1 (
  input  I0,
  input  I1,
  input  I2,
  input  I3,
  input  I4,
  input  I5,
  input  I6,
  input  I7,
  output O
);

  wire and_1_out, and_2_out, and_3_out;

  and and_1 (and_1_out, I0, I1);
  and and_2 (and_2_out, I2, I3);
  and and_3 (and_3_out, I4, I5, I6, ~I7);  // And
  or or_1 (O, and_1_out, and_2_out, and_3_out);
endmodule
