// Digital circuit ET3+1.dig as structural Verilog
module ET3_1 (
  input  I0,
  input  I1,
  input  I2,
  input  I3,
  output O
);

  wire and_1_out, and_2_out;

  and and_1 (and_1_out, I0, I1);
  and and_2 (and_2_out, I2, I3);
  or or_1 (O, and_1_out, and_2_out);
endmodule
