// Digital circuit S1e3.dig as structural Verilog
module S1e3 (
  input  I0,
  input  I1,
  input  I2,
  input  I3,
  input  I4,
  input  I5,
  output Verm,
  output Amar,
  output Verd
);

  and and_1 (Amar, I0, I1, I2);
  and and_2 (Verd, I3, I4, I5);
  and and_3 (Verm, ~Amar, ~Verd);  // And
endmodule
