// Digital circuit S2.dig as structural Verilog
module S2 (
  input  I0,
  input  I1,
  input  I2,
  input  I3,
  output Verm,
  output Amar,
  output Verd
);

  and and_1 (Amar, I0, I1);
  and and_2 (Verd, I2, I3);
  and and_3 (Verm, ~Amar, ~Verd);  // And
endmodule
