// Digital circuit TrabalhoFinal.dig as structural Verilog
module TrabalhoFinal (
  input  CLK
);

  wire and_1_out, \Botão_out , Estado_1_nq, Estado_1_q, Estado_2_nq, Estado_2_q, Estado_3_nq, Estado_3_q,
       et2_1_1_o, et3_1_1_o, not_1_out, not_2_out, s1e3_1_amar, s1e3_1_verd, s1e3_1_verm, s1e3_2_amar,
       s1e3_2_verd, s1e3_2_verm, s2_1_amar, s2_1_verd, s2_1_verm, \SR_de_sincronização_q ;

  Button \Botão  (.out(\Botão_out ));
  RS_FF_AS \SR_de_sincronização  (.S(\Botão_out ), .R(Estado_1_q), .Q(\SR_de_sincronização_q ));  // open: nQ
  LED \Semáforo_1  (.in(s1e3_1_verm));
  LED led_1 (.in(s1e3_1_amar));
  LED led_2 (.in(s1e3_1_verd));
  S1e3 s1e3_1 (
    .I0(Estado_3_q), .I1(Estado_1_nq), .I2(Estado_2_nq), .I3(Estado_3_nq), .I4(Estado_1_nq),
    .I5(Estado_2_nq), .Verm(s1e3_1_verm), .Amar(s1e3_1_amar), .Verd(s1e3_1_verd));
  and and_1 (and_1_out, Estado_1_nq, Estado_3_q, \SR_de_sincronização_q );
  ET2_1 et2_1_1 (
    .I0(Estado_2_q), .I1(Estado_3_nq), .I2(Estado_1_q), .I3(Estado_3_nq), .I4(Estado_1_nq), .I5(Estado_2_nq),
    .I6(Estado_3_q), .I7(\SR_de_sincronização_q ), .O(et2_1_1_o));
  ET3_1 et3_1_1 (.I0(Estado_3_nq), .I1(Estado_1_nq), .I2(\SR_de_sincronização_q ), .I3(Estado_2_q), .O(et3_1_1_o));
  S2 s2_1 (
    .I0(Estado_3_q), .I1(Estado_2_q), .I2(Estado_3_nq), .I3(Estado_2_q), .Verm(s2_1_verm), .Amar(s2_1_amar),
    .Verd(s2_1_verd));
  LED \Semáforo_2  (.in(s2_1_verm));
  LED led_3 (.in(s2_1_amar));
  LED led_4 (.in(s2_1_verd));
  S1e3 s1e3_2 (
    .I0(Estado_3_q), .I1(Estado_1_nq), .I2(Estado_2_nq), .I3(Estado_3_nq), .I4(Estado_1_nq),
    .I5(Estado_2_nq), .Verm(s1e3_2_verm), .Amar(s1e3_2_amar), .Verd(s1e3_2_verd));
  LED \Semáforo_3  (.in(s1e3_2_verm));
  LED led_5 (.in(s1e3_2_amar));
  LED led_6 (.in(s1e3_2_verd));
  LED \Semáforo_4  (.in(not_1_out));
  not not_1 (not_1_out, Estado_1_q);
  LED led_7 (.in(Estado_1_q));
  LED \Semáforo_5  (.in(not_2_out));
  not not_2 (not_2_out, Estado_1_q);
  LED led_8 (.in(Estado_1_q));
  D_FF Estado_1 (.D(and_1_out), .C(CLK), .Q(Estado_1_q), .nQ(Estado_1_nq));
  D_FF Estado_2 (.D(et2_1_1_o), .C(CLK), .Q(Estado_2_q), .nQ(Estado_2_nq));
  D_FF Estado_3 (.D(et3_1_1_o), .C(CLK), .Q(Estado_3_q), .nQ(Estado_3_nq));
endmodule
